# Fritzing sketch distancemusic (saved by Fritzing 0.9.3b)
circuit board: 8.46667cm x 5.64444cm
breadboards: 1

parts:
  Bauteil1 = Arduino Uno (Rev3)
  J1 = Piezo Speaker
  J3 = Piezo Speaker
  LED2 = LED - 5mm [color="Yellow (592nm)" package="5 mm [THT]"]
  LED3 = LED - 5mm [color="Red (633nm)" package="5 mm [THT]"]
  LED1 = smd LED [color="Green (560nm)" package="1206 [SMD]"]
  S1 = Pushbutton [package="[THT]"]
  R1 = Resistor [tolerance=±5% resistance=220 package=THT]
  R2 = Resistor [tolerance=±5% resistance=220 package=THT]
  R3 = Resistor [tolerance=±5% resistance=220 package=THT]
  HC-SR04_Sensor_1 = HC-SR04 Ultrasonic Distance Sensor
  U1 = POT [package=pot_mammoth]

nets:
  N1: Bauteil1.A0, U1.A
  N2: Bauteil1.D8, J3.pin2
  N3: Bauteil1.D9_PWM, J1.pin2
  N4: Bauteil1.D11_PWM/MOSI, HC-SR04_Sensor_1.ECHO
  N5: Bauteil1.D12/MISO, HC-SR04_Sensor_1.TRIG
  N6: Bauteil1.D2, S1.Pin_3, S1.Pin_4
  N7: Bauteil1.D3_PWM, LED3.cathode
  N8: Bauteil1.D4, LED2.cathode
  N9: Bauteil1.D5_PWM, LED1.cathode
  5V: Bauteil1.5V, HC-SR04_Sensor_1.VCC, U1.S
  GND: Bauteil1.GND, J1.pin1, J3.pin1, S1.Pin_1, S1.Pin_2, R1.Pin_1, R2.Pin_1, R3.Pin_1, HC-SR04_Sensor_1.GND, U1.E
  N10: LED2.anode, R2.Pin_0
  N11: LED3.anode, R1.Pin_0
  N12: LED1.anode, R3.Pin_0
